// Logisim project HW3.circ as structural Verilog: 4 circuits, main circuit 16-bit ALU
module _1_bit_Full_Adder (
  input  A,
  input  B,
  input  CarryIn,
  output Answer,
  output CarryOut
);

  wire and_2_out, and_3_out, and_4_out, and_5_out, and_6_out, and_7_out, and_8_out;

  // AND_Gate and_1 has open pins: in0=A, in1=B, in2=CarryIn, out=open
  and and_2 (and_2_out, ~A, ~B, CarryIn);  // AND_Gate
  and and_3 (and_3_out, ~A, B, ~CarryIn);  // AND_Gate
  and and_4 (and_4_out, ~A, B, CarryIn);  // AND_Gate
  and and_5 (and_5_out, A, ~B, ~CarryIn);  // AND_Gate
  and and_6 (and_6_out, A, ~B, CarryIn);  // AND_Gate
  and and_7 (and_7_out, A, B, ~CarryIn);  // AND_Gate
  and and_8 (and_8_out, A, B, CarryIn);
  or or_1 (CarryOut, and_4_out, and_6_out, and_7_out, and_8_out);
  or or_2 (Answer, and_8_out, and_2_out, and_3_out, and_5_out);

  // Notes on the sheet:
  //   Shen Yang
  //   2/1/2014
  //   1-bit Full Adder
endmodule

module _4_bit_Full_Adder (
  input  [3:0] B,
  input  [3:0] A,
  input  CarryIn,
  output CarryOut,
  output [3:0] Answer
);

  wire _1_bit_2_carryout, _1_bit_3_carryout, _1_bit_4_carryout;

  _1_bit_Full_Adder _1_bit (.A(A[3]), .B(B[3]), .CarryIn(_1_bit_2_carryout), .Answer(Answer[3]), .CarryOut(CarryOut));
  _1_bit_Full_Adder _1_bit_2 (
    .A(A[2]), .B(B[2]), .CarryIn(_1_bit_3_carryout), .Answer(Answer[2]), .CarryOut(_1_bit_2_carryout));
  _1_bit_Full_Adder _1_bit_3 (
    .A(A[1]), .B(B[1]), .CarryIn(_1_bit_4_carryout), .Answer(Answer[1]), .CarryOut(_1_bit_3_carryout));
  _1_bit_Full_Adder _1_bit_4 (.A(A[0]), .B(B[0]), .CarryIn(CarryIn), .Answer(Answer[0]), .CarryOut(_1_bit_4_carryout));

  // Notes on the sheet:
  //   Shen Yang
  //   2/1/2014
  //   4-bit Full Adder
endmodule

module _4_bit_ALU (
  input  [3:0] A,
  input  [3:0] B,
  input  CarryIn,
  input  S2,
  input  S1,
  input  S0,
  output [3:0] out_7,
  output CarryOut
);

  wire n4_bit_full_adder_1_carryout, n4_bit_full_adder_2_carryout, n4_bit_full_adder_3_carryout,
       n4_bit_full_adder_4_carryout, not_2_out;
  wire [3:0] and_1_out, n4_bit_full_adder_1_answer, n4_bit_full_adder_2_answer, n4_bit_full_adder_3_answer,
       n4_bit_full_adder_4_answer, not_1_out, not_3_out, or_1_out, xor_1_out;

  _4_bit_Full_Adder u_4_bit_full_adder_1 (
    .B(B), .CarryOut(n4_bit_full_adder_1_carryout), .A(A), .Answer(n4_bit_full_adder_1_answer),
    .CarryIn(CarryIn));
  assign not_1_out = ~B;  // NOT_Gate not_1, 4 bits wide
  _4_bit_Full_Adder u_4_bit_full_adder_2 (
    .B(not_1_out), .CarryOut(n4_bit_full_adder_2_carryout), .A(A), .Answer(n4_bit_full_adder_2_answer),
    .CarryIn(not_2_out));
  not not_2 (not_2_out, CarryIn);
  _4_bit_Full_Adder u_4_bit_full_adder_3 (
    .B(B), .CarryOut(n4_bit_full_adder_3_carryout), .A(A), .Answer(n4_bit_full_adder_3_answer),
    .CarryIn(not_2_out));
  assign not_3_out = ~A;  // NOT_Gate not_3, 4 bits wide
  _4_bit_Full_Adder u_4_bit_full_adder_4 (
    .B(B), .CarryOut(n4_bit_full_adder_4_carryout), .A(not_3_out), .Answer(n4_bit_full_adder_4_answer),
    .CarryIn(not_2_out));
  assign and_1_out = A & B;  // AND_Gate and_1, 4 bits wide
  assign xor_1_out = A ^ B;  // XOR_Gate xor_1, 4 bits wide
  assign or_1_out = A | B;  // OR_Gate or_1, 4 bits wide
  Multiplexer #(.select(3), .disabled(0), .enable("false")) multiplexer_1 (
    .in0(n4_bit_full_adder_1_carryout), .in1(n4_bit_full_adder_2_carryout),
    .in2(n4_bit_full_adder_3_carryout), .in3(n4_bit_full_adder_4_carryout), .in4(CarryIn), .in5(CarryIn),
    .in6(CarryIn), .in7(CarryIn), .out(CarryOut), .sel({S2, S1, S0}));
  Multiplexer #(.select(3), .width(4), .disabled(0), .enable("false")) multiplexer_2 (
    .in0(n4_bit_full_adder_1_answer), .in1(n4_bit_full_adder_2_answer), .in2(n4_bit_full_adder_3_answer),
    .in3(n4_bit_full_adder_4_answer), .in4(and_1_out), .in5(or_1_out), .in6(not_3_out), .in7(xor_1_out),
    .out(out_7), .sel({S2, S1, S0}));

  // Other names for the same wires on the sheet: Answer[3:0] = out_7; Selector[2:0] = {S2, S1, S0}

  // Notes on the sheet:
  //   Shen Yang
  //   2/1/2014
  //   4-bit ALU
  //   000 = Addition
  //   001 = Subtraction
  //   010 = Increment
  //   011 = Negation
  //   100 = AND
  //   101 = OR
  //   110 = NOT
  //   111 = XOR
endmodule

module _16_bit_ALU (
  input  S2,
  input  S1,
  input  S0,
  input  [15:0] A,
  input  [15:0] B,
  input  CarryIn,
  input  [3:0] in_7,
  input  [3:0] in_8,
  input  [3:0] in_9,
  input  [3:0] in_10,
  output [15:0] out_11
);

  wire n4_bit_full_adder_1_carryout, n4_bit_full_adder_2_carryout, n4_bit_full_adder_3_carryout,
       n4_bit_full_adder_4_carryout, n4_bit_full_adder_5_carryout, n4_bit_full_adder_6_carryout,
       n4_bit_full_adder_9_carryout, n4_bit_full_adder_10_carryout, n4_bit_full_adder_11_carryout,
       n4_bit_full_adder_13_carryout, n4_bit_full_adder_14_carryout, n4_bit_full_adder_15_carryout,
       n4_bit_full_adder_16_carryout, n4_bit_full_adder_17_carryout, n4_bit_full_adder_18_carryout, not_5_out;
  wire [3:0] n4_bit_alu_1_out_7, n4_bit_alu_2_out_7, n4_bit_alu_3_out_7, n4_bit_alu_4_out_7,
       n4_bit_full_adder_1_answer, n4_bit_full_adder_2_answer, n4_bit_full_adder_3_answer,
       n4_bit_full_adder_4_answer, n4_bit_full_adder_5_answer, n4_bit_full_adder_6_answer,
       n4_bit_full_adder_7_answer, n4_bit_full_adder_8_answer, n4_bit_full_adder_9_answer,
       n4_bit_full_adder_13_answer, n4_bit_full_adder_14_answer, n4_bit_full_adder_17_answer,
       n4_bit_full_adder_18_answer, n4_bit_full_adder_19_answer, n4_bit_full_adder_20_answer, not_1_out,
       not_2_out, not_3_out, not_4_out, not_6_out, not_7_out, not_8_out, not_9_out;
  wire [7:0] n4_bit_full_adder_16_answer;
  wire [15:4] n4_bit_full_adder_10_answer;

  assign not_1_out = ~B[3:0];  // NOT_Gate not_1, 4 bits wide
  assign not_2_out = ~B[7:4];  // NOT_Gate not_2, 4 bits wide
  _4_bit_Full_Adder u_4_bit_full_adder_1 (
    .B(not_1_out), .CarryOut(n4_bit_full_adder_1_carryout), .A(A[3:0]), .Answer(n4_bit_full_adder_1_answer),
    .CarryIn(CarryIn));
  assign not_3_out = ~B[11:8];  // NOT_Gate not_3, 4 bits wide
  assign not_4_out = ~B[15:12];  // NOT_Gate not_4, 4 bits wide
  _4_bit_Full_Adder u_4_bit_full_adder_2 (
    .B(in_9), .CarryOut(n4_bit_full_adder_2_carryout), .A(n4_bit_full_adder_1_answer),
    .Answer(n4_bit_full_adder_2_answer), .CarryIn(not_5_out));
  _4_bit_Full_Adder u_4_bit_full_adder_3 (
    .B(not_2_out), .CarryOut(n4_bit_full_adder_3_carryout), .A(A[7:4]), .Answer(n4_bit_full_adder_3_answer),
    .CarryIn(n4_bit_full_adder_1_carryout));
  _4_bit_Full_Adder u_4_bit_full_adder_4 (
    .B(in_9), .CarryOut(n4_bit_full_adder_4_carryout), .A(n4_bit_full_adder_3_answer),
    .Answer(n4_bit_full_adder_4_answer), .CarryIn(n4_bit_full_adder_2_carryout));
  _4_bit_Full_Adder u_4_bit_full_adder_5 (
    .B(not_3_out), .CarryOut(n4_bit_full_adder_5_carryout), .A(A[11:8]), .Answer(n4_bit_full_adder_5_answer),
    .CarryIn(n4_bit_full_adder_3_carryout));
  _4_bit_Full_Adder u_4_bit_full_adder_6 (
    .B(in_9), .CarryOut(n4_bit_full_adder_6_carryout), .A(n4_bit_full_adder_5_answer),
    .Answer(n4_bit_full_adder_6_answer), .CarryIn(n4_bit_full_adder_4_carryout));
  _4_bit_Full_Adder u_4_bit_full_adder_7 (
    .B(not_4_out), .A(A[15:12]), .Answer(n4_bit_full_adder_7_answer), .CarryIn(n4_bit_full_adder_5_carryout));  // open: CarryOut
  _4_bit_Full_Adder u_4_bit_full_adder_8 (
    .B(in_9), .A(n4_bit_full_adder_7_answer), .Answer(n4_bit_full_adder_8_answer),
    .CarryIn(n4_bit_full_adder_6_carryout));  // open: CarryOut
  _4_bit_ALU u_4_bit_alu_1 (
    .A(A[3:0]), .B(B[3:0]), .CarryIn(CarryIn), .S2(S2), .S1(S1), .S0(S0), .out_7(n4_bit_alu_1_out_7));  // open: CarryOut
  _4_bit_ALU u_4_bit_alu_2 (
    .A(A[7:4]), .B(B[7:4]), .CarryIn(CarryIn), .S2(S2), .S1(S1), .S0(S0), .out_7(n4_bit_alu_2_out_7));  // open: CarryOut
  _4_bit_ALU u_4_bit_alu_3 (
    .A(A[11:8]), .B(B[11:8]), .CarryIn(CarryIn), .S2(S2), .S1(S1), .S0(S0), .out_7(n4_bit_alu_3_out_7));  // open: CarryOut
  _4_bit_ALU u_4_bit_alu_4 (
    .A(A[15:12]), .B(B[15:12]), .CarryIn(CarryIn), .S2(S2), .S1(S1), .S0(S0), .out_7(n4_bit_alu_4_out_7));  // open: CarryOut
  not not_5 (not_5_out, CarryIn);
  _4_bit_Full_Adder u_4_bit_full_adder_9 (
    .B(in_7), .CarryOut(n4_bit_full_adder_9_carryout), .A(A[3:0]), .Answer(n4_bit_full_adder_9_answer),
    .CarryIn(not_5_out));
  _4_bit_Full_Adder u_4_bit_full_adder_10 (
    .B(in_7), .CarryOut(n4_bit_full_adder_10_carryout), .A(A[7:4]),
    .Answer(n4_bit_full_adder_10_answer[7:4]), .CarryIn(n4_bit_full_adder_9_carryout));
  _4_bit_Full_Adder u_4_bit_full_adder_11 (
    .B(in_7), .CarryOut(n4_bit_full_adder_11_carryout), .A(A[11:8]),
    .Answer(n4_bit_full_adder_10_answer[11:8]), .CarryIn(n4_bit_full_adder_10_carryout));
  _4_bit_Full_Adder u_4_bit_full_adder_12 (
    .B(in_7), .A(A[15:12]), .Answer(n4_bit_full_adder_10_answer[15:12]),
    .CarryIn(n4_bit_full_adder_11_carryout));  // open: CarryOut
  Multiplexer #(.select(3), .width(16), .disabled(0), .enable("false")) multiplexer_1 (
    .in0({n4_bit_alu_4_out_7, n4_bit_alu_3_out_7, n4_bit_alu_2_out_7, n4_bit_alu_1_out_7}),
    .in1({n4_bit_full_adder_8_answer, n4_bit_full_adder_6_answer, n4_bit_full_adder_4_answer, n4_bit_full_adder_2_answer}),
    .in2({n4_bit_full_adder_10_answer, n4_bit_full_adder_9_answer}),
    .in3({n4_bit_full_adder_20_answer, n4_bit_full_adder_18_answer, n4_bit_full_adder_16_answer}),
    .in4({n4_bit_alu_4_out_7, n4_bit_alu_3_out_7, n4_bit_alu_2_out_7, n4_bit_alu_1_out_7}),
    .in5({n4_bit_alu_4_out_7, n4_bit_alu_3_out_7, n4_bit_alu_2_out_7, n4_bit_alu_1_out_7}),
    .in6({n4_bit_alu_4_out_7, n4_bit_alu_3_out_7, n4_bit_alu_2_out_7, n4_bit_alu_1_out_7}),
    .in7({n4_bit_alu_4_out_7, n4_bit_alu_3_out_7, n4_bit_alu_2_out_7, n4_bit_alu_1_out_7}), .out(out_11),
    .sel({S2, S1, S0}));
  assign not_6_out = ~A[3:0];  // NOT_Gate not_6, 4 bits wide
  assign not_7_out = ~A[7:4];  // NOT_Gate not_7, 4 bits wide
  _4_bit_Full_Adder u_4_bit_full_adder_13 (
    .B(in_8), .CarryOut(n4_bit_full_adder_13_carryout), .A(not_6_out), .Answer(n4_bit_full_adder_13_answer),
    .CarryIn(CarryIn));
  _4_bit_Full_Adder u_4_bit_full_adder_14 (
    .B(in_8), .CarryOut(n4_bit_full_adder_14_carryout), .A(not_7_out), .Answer(n4_bit_full_adder_14_answer),
    .CarryIn(n4_bit_full_adder_13_carryout));
  _4_bit_Full_Adder u_4_bit_full_adder_15 (
    .B(in_10), .CarryOut(n4_bit_full_adder_15_carryout), .A(n4_bit_full_adder_14_answer),
    .Answer(n4_bit_full_adder_16_answer[7:4]), .CarryIn(n4_bit_full_adder_16_carryout));
  _4_bit_Full_Adder u_4_bit_full_adder_16 (
    .B(in_10), .CarryOut(n4_bit_full_adder_16_carryout), .A(n4_bit_full_adder_13_answer),
    .Answer(n4_bit_full_adder_16_answer[3:0]), .CarryIn(not_5_out));
  assign not_8_out = ~A[11:8];  // NOT_Gate not_8, 4 bits wide
  _4_bit_Full_Adder u_4_bit_full_adder_17 (
    .B(in_8), .CarryOut(n4_bit_full_adder_17_carryout), .A(not_8_out), .Answer(n4_bit_full_adder_17_answer),
    .CarryIn(n4_bit_full_adder_14_carryout));
  _4_bit_Full_Adder u_4_bit_full_adder_18 (
    .B(in_10), .CarryOut(n4_bit_full_adder_18_carryout), .A(n4_bit_full_adder_17_answer),
    .Answer(n4_bit_full_adder_18_answer), .CarryIn(n4_bit_full_adder_15_carryout));
  assign not_9_out = ~A[15:12];  // NOT_Gate not_9, 4 bits wide
  _4_bit_Full_Adder u_4_bit_full_adder_19 (
    .B(in_8), .A(not_9_out), .Answer(n4_bit_full_adder_19_answer), .CarryIn(n4_bit_full_adder_17_carryout));  // open: CarryOut
  _4_bit_Full_Adder u_4_bit_full_adder_20 (
    .B(in_10), .A(n4_bit_full_adder_19_answer), .Answer(n4_bit_full_adder_20_answer),
    .CarryIn(n4_bit_full_adder_18_carryout));  // open: CarryOut

  // Other names for the same wires on the sheet: A0[3:0] = A[3:0]; A1[3:0] = A[7:4]; A2[3:0] = A[11:8];
  //   A3[3:0] = A[15:12]; Answer[15:0] = out_11; B0[3:0] = B[3:0]; B1[3:0] = B[7:4]; B2[3:0] = B[11:8];
  //   B3[3:0] = B[15:12]

  // Notes on the sheet:
  //   Shen Yang
  //   2/1/2014
  //   16-bit ALU
  //   000 = Addition
  //   001 = Subtraction
  //   010 = Increment
  //   011 = Negation
  //   100 = AND
  //   101 = OR
  //   110 = NOT
  //   111 = XOR
endmodule
