// Logisim project lab3.circ as structural Verilog: 4 circuits, main circuit demorgans
module demorgans (
  input  in_1,
  input  in_2,
  output out_3,
  output out_4
);


  // Other names for the same wires on the sheet: A = in_1; B = in_2; U = out_3; V = out_4
endmodule

module NAND (
  input  A,
  input  B,
  output Q
);
endmodule

module NOT (
  input  A,
  output Q
);
endmodule

module AND (
  input  A,
  input  B,
  output Q
);
endmodule
