// Logisim project timedlab1.circ as structural Verilog: 2 circuits, main circuit main
module main (
  input  NICE
);

  wire POLITE, W1, W2, W3, W4;
  wire [6:0] tlm1_1__3e, tlm1_1__7f, tlm1_1__40, tlm1_1__41, tlm2a_1__7f, tlm2a_1__08, tlm2a_1__49,
       tlm2b_1_out_3, tlm2b_1_out_4, tlm2b_1_out_5, tlm2b_1_out_6, tlm2b_1_out_7, tlm2c_1_out_3,
       tlm2c_1_out_4, tlm2c_1_out_5, tlm2c_1_out_6, tlm2c_1_out_7, tlm3_1__01, tlm3_1__1e, tlm3_1__7e,
       tlm3_1__7f, tlm3_1__08, tlm3_1__40, tlm3_1__41, tlm4_1__2e, tlm4_1__3e, tlm4_1__3f, tlm4_1__41,
       tlm4_1__48, tlm4_1__49;

  Button RESET ();  // open: out
  Clock CLOCK ();  // open: out
  DotMatrix dotmatrix_1 (.col0(tlm1_1__40), .col1(tlm1_1__40), .col2(tlm1_1__7f), .col3(tlm1_1__40), .col4(tlm1_1__40));
  TLM1 tlm1_1 (.WORD(W1), ._40(tlm1_1__40), ._7f(tlm1_1__7f), ._3e(tlm1_1__3e), ._41(tlm1_1__41));
  DotMatrix dotmatrix_2 (.col0(tlm3_1__7e), .col1(tlm3_1__01), .col2(tlm3_1__1e), .col3(tlm3_1__01), .col4(tlm3_1__7e));
  TLM3 tlm3_1 (
    .WORD(W3), ._7e(tlm3_1__7e), ._01(tlm3_1__01), ._1e(tlm3_1__1e), ._41(tlm3_1__41), ._7f(tlm3_1__7f),
    ._40(tlm3_1__40), ._08(tlm3_1__08));
  DotMatrix dotmatrix_3 (.col0(tlm1_1__3e), .col1(tlm1_1__41), .col2(tlm1_1__41), .col3(tlm1_1__41), .col4(tlm1_1__3e));
  DotMatrix dotmatrix_4 (.col0(tlm3_1__41), .col1(tlm3_1__41), .col2(tlm3_1__7f), .col3(tlm3_1__41), .col4(tlm3_1__41));
  DotMatrix dotmatrix_5 (.col0(tlm3_1__40), .col1(tlm3_1__40), .col2(tlm3_1__7f), .col3(tlm3_1__40), .col4(tlm3_1__40));
  DotMatrix dotmatrix_6 (
    .col0(tlm2a_1__7f), .col1(tlm2a_1__08), .col2(tlm2a_1__08), .col3(tlm2a_1__08), .col4(tlm2a_1__7f));
  TLM2a tlm2a_1 (.WORD(W2), ._7f(tlm2a_1__7f), ._08(tlm2a_1__08), ._49(tlm2a_1__49));
  DotMatrix dotmatrix_7 (.col0(tlm3_1__7f), .col1(tlm3_1__08), .col2(tlm3_1__08), .col3(tlm3_1__08), .col4(tlm3_1__7f));
  DotMatrix dotmatrix_8 (
    .col0(tlm2a_1__7f), .col1(tlm2a_1__49), .col2(tlm2a_1__49), .col3(tlm2a_1__49), .col4(tlm2a_1__49));
  TLM4 tlm4_1 (
    .WORD(W4), ._3e(tlm4_1__3e), ._41(tlm4_1__41), ._49(tlm4_1__49), ._2e(tlm4_1__2e), ._3f(tlm4_1__3f),
    ._48(tlm4_1__48));
  DotMatrix dotmatrix_9 (
    .col0(tlm2b_1_out_3), .col1(tlm2b_1_out_4), .col2(tlm2b_1_out_5), .col3(tlm2b_1_out_6),
    .col4(tlm2b_1_out_7));
  DotMatrix dotmatrix_10 (
    .col0(tlm2c_1_out_3), .col1(tlm2c_1_out_4), .col2(tlm2c_1_out_5), .col3(tlm2c_1_out_6),
    .col4(tlm2c_1_out_7));
  TLM2c tlm2c_1 (
    .out_3(tlm2c_1_out_3), .out_4(tlm2c_1_out_4), .out_5(tlm2c_1_out_5), .out_6(tlm2c_1_out_6),
    .out_7(tlm2c_1_out_7), .WORD(W2), .NICE(POLITE));
  TLM2b tlm2b_1 (
    .out_3(tlm2b_1_out_3), .out_4(tlm2b_1_out_4), .out_5(tlm2b_1_out_5), .out_6(tlm2b_1_out_6),
    .out_7(tlm2b_1_out_7), .WORD(W2), .NICE(POLITE));
  DotMatrix dotmatrix_11 (
    .col0(tlm4_1__3f), .col1(tlm4_1__48), .col2(tlm4_1__48), .col3(tlm4_1__48), .col4(tlm4_1__3f));
  DotMatrix dotmatrix_12 (
    .col0(tlm4_1__3e), .col1(tlm4_1__41), .col2(tlm4_1__49), .col3(tlm4_1__49), .col4(tlm4_1__2e));
endmodule

module statemachine (
);


  // Notes on the sheet:
  //   Build your state machine here
endmodule
