// Logisim project timedlab1lib.circ as structural Verilog: 6 circuits, main circuit TLM1
module TLM1 (
  input  WORD,
  output [6:0] _40,
  output [6:0] _7f,
  output [6:0] _3e,
  output [6:0] _41
);

  Multiplexer #(.select(1), .width(7)) multiplexer_1 (.in0({7{1'b0}}), .in1(7'b1000000), .out(_40), .sel(WORD));
  Multiplexer #(.select(1), .width(7)) multiplexer_2 (.in0({7{1'b0}}), .in1({7{1'b1}}), .out(_7f), .sel(WORD));
  Multiplexer #(.select(1), .width(7)) multiplexer_3 (.in0({7{1'b0}}), .in1(7'b0111110), .out(_3e), .sel(WORD));
  Multiplexer #(.select(1), .width(7)) multiplexer_4 (.in0({7{1'b0}}), .in1(7'b1000001), .out(_41), .sel(WORD));
endmodule

module TLM2a (
  input  WORD,
  output [6:0] _7f,
  output [6:0] _08,
  output [6:0] _49
);

  Multiplexer #(.select(1), .width(7)) multiplexer_1 (.in0({7{1'b0}}), .in1({7{1'b1}}), .out(_7f), .sel(WORD));
  Multiplexer #(.select(1), .width(7)) multiplexer_2 (.in0({7{1'b0}}), .in1(7'b0001000), .out(_08), .sel(WORD));
  Multiplexer #(.select(1), .width(7)) multiplexer_3 (.in0({7{1'b0}}), .in1(7'b1001001), .out(_49), .sel(WORD));
endmodule

module TLM2b (
  input  WORD,
  input  NICE,
  output [6:0] out_3,
  output [6:0] out_4,
  output [6:0] out_5,
  output [6:0] out_6,
  output [6:0] out_7
);

  wire [6:0] multiplexer_2_out, multiplexer_4_out, multiplexer_6_out, multiplexer_8_out, multiplexer_10_out;

  Multiplexer #(.select(1), .width(7)) multiplexer_1 (
    .in0({7{1'b0}}), .in1(multiplexer_2_out), .out(out_3), .sel(WORD));
  Multiplexer #(.select(1), .width(7)) multiplexer_2 (
    .in0({7{1'b1}}), .in1(7'b0111110), .out(multiplexer_2_out), .sel(NICE));
  Multiplexer #(.select(1), .width(7)) multiplexer_3 (
    .in0({7{1'b0}}), .in1(multiplexer_4_out), .out(out_4), .sel(WORD));
  Multiplexer #(.select(1), .width(7)) multiplexer_4 (
    .in0(7'b0000001), .in1(7'b1000001), .out(multiplexer_4_out), .sel(NICE));
  Multiplexer #(.select(1), .width(7)) multiplexer_5 (
    .in0({7{1'b0}}), .in1(multiplexer_6_out), .out(out_5), .sel(WORD));
  Multiplexer #(.select(1), .width(7)) multiplexer_6 (
    .in0(7'b0000001), .in1(7'b1000001), .out(multiplexer_6_out), .sel(NICE));
  Multiplexer #(.select(1), .width(7)) multiplexer_7 (
    .in0({7{1'b0}}), .in1(multiplexer_8_out), .out(out_6), .sel(WORD));
  Multiplexer #(.select(1), .width(7)) multiplexer_8 (
    .in0(7'b0000001), .in1(7'b1000001), .out(multiplexer_8_out), .sel(NICE));
  Multiplexer #(.select(1), .width(7)) multiplexer_9 (
    .in0({7{1'b0}}), .in1(multiplexer_10_out), .out(out_7), .sel(WORD));
  Multiplexer #(.select(1), .width(7)) multiplexer_10 (
    .in0(7'b0000001), .in1(7'b0100010), .out(multiplexer_10_out), .sel(NICE));
endmodule

module TLM2c (
  input  WORD,
  input  NICE,
  output [6:0] out_3,
  output [6:0] out_4,
  output [6:0] out_5,
  output [6:0] out_6,
  output [6:0] out_7
);

  wire [6:0] multiplexer_2_out, multiplexer_4_out, multiplexer_6_out, multiplexer_8_out, multiplexer_10_out;

  Multiplexer #(.select(1), .width(7)) multiplexer_1 (
    .in0({7{1'b0}}), .in1(multiplexer_2_out), .out(out_3), .sel(WORD));
  Multiplexer #(.select(1), .width(7)) multiplexer_2 (
    .in0({7{1'b1}}), .in1({7{1'b1}}), .out(multiplexer_2_out), .sel(NICE));
  Multiplexer #(.select(1), .width(7)) multiplexer_3 (
    .in0({7{1'b0}}), .in1(multiplexer_4_out), .out(out_4), .sel(WORD));
  Multiplexer #(.select(1), .width(7)) multiplexer_4 (
    .in0(7'b0000001), .in1(7'b0001000), .out(multiplexer_4_out), .sel(NICE));
  Multiplexer #(.select(1), .width(7)) multiplexer_5 (
    .in0({7{1'b0}}), .in1(multiplexer_6_out), .out(out_5), .sel(WORD));
  Multiplexer #(.select(1), .width(7)) multiplexer_6 (
    .in0(7'b0000001), .in1(7'b0010100), .out(multiplexer_6_out), .sel(NICE));
  Multiplexer #(.select(1), .width(7)) multiplexer_7 (
    .in0({7{1'b0}}), .in1(multiplexer_8_out), .out(out_6), .sel(WORD));
  Multiplexer #(.select(1), .width(7)) multiplexer_8 (
    .in0(7'b0000001), .in1(7'b0100010), .out(multiplexer_8_out), .sel(NICE));
  Multiplexer #(.select(1), .width(7)) multiplexer_9 (
    .in0({7{1'b0}}), .in1(multiplexer_10_out), .out(out_7), .sel(WORD));
  Multiplexer #(.select(1), .width(7)) multiplexer_10 (
    .in0(7'b0000001), .in1(7'b1000001), .out(multiplexer_10_out), .sel(NICE));
endmodule

module TLM3 (
  input  WORD,
  output [6:0] _7e,
  output [6:0] _01,
  output [6:0] _1e,
  output [6:0] _41,
  output [6:0] _7f,
  output [6:0] _40,
  output [6:0] _08
);

  Multiplexer #(.select(1), .width(7)) multiplexer_1 (.in0({7{1'b0}}), .in1(7'b1111110), .out(_7e), .sel(WORD));
  Multiplexer #(.select(1), .width(7)) multiplexer_2 (.in0({7{1'b0}}), .in1(7'b0000001), .out(_01), .sel(WORD));
  Multiplexer #(.select(1), .width(7)) multiplexer_3 (.in0({7{1'b0}}), .in1(7'b0011110), .out(_1e), .sel(WORD));
  Multiplexer #(.select(1), .width(7)) multiplexer_4 (.in0({7{1'b0}}), .in1(7'b1000001), .out(_41), .sel(WORD));
  Multiplexer #(.select(1), .width(7)) multiplexer_5 (.in0({7{1'b0}}), .in1({7{1'b1}}), .out(_7f), .sel(WORD));
  Multiplexer #(.select(1), .width(7)) multiplexer_6 (.in0({7{1'b0}}), .in1(7'b1000000), .out(_40), .sel(WORD));
  Multiplexer #(.select(1), .width(7)) multiplexer_7 (.in0({7{1'b0}}), .in1(7'b0001000), .out(_08), .sel(WORD));
endmodule

module TLM4 (
  input  WORD,
  output [6:0] _3e,
  output [6:0] _41,
  output [6:0] _49,
  output [6:0] _2e,
  output [6:0] _3f,
  output [6:0] _48
);

  Multiplexer #(.select(1), .width(7)) multiplexer_1 (.in0({7{1'b0}}), .in1(7'b0111110), .out(_3e), .sel(WORD));
  Multiplexer #(.select(1), .width(7)) multiplexer_2 (.in0({7{1'b0}}), .in1(7'b1000001), .out(_41), .sel(WORD));
  Multiplexer #(.select(1), .width(7)) multiplexer_3 (.in0({7{1'b0}}), .in1(7'b1001001), .out(_49), .sel(WORD));
  Multiplexer #(.select(1), .width(7)) multiplexer_4 (.in0({7{1'b0}}), .in1(7'b0101110), .out(_2e), .sel(WORD));
  Multiplexer #(.select(1), .width(7)) multiplexer_5 (.in0({7{1'b0}}), .in1(7'b0111111), .out(_3f), .sel(WORD));
  Multiplexer #(.select(1), .width(7)) multiplexer_6 (.in0({7{1'b0}}), .in1(7'b1001000), .out(_48), .sel(WORD));
endmodule
